// Logisim project LC-3.circ as structural Verilog: 4 circuits, main circuit main_2
module main_2 (
  output [15:0] PC_OUT,
  output out_2,
  output out_3,
  output [15:0] IR_OUT,
  output out_5,
  output [3:0] out_6,
  output [1:0] out_7,
  output out_8,
  output [1:0] out_9,
  output out_10,
  output [2:0] out_11,
  output out_12,
  output [2:0] out_13,
  output [2:0] out_14,
  output [8:0] out_15,
  output [5:0] out_16,
  output [2:0] out_17,
  output [2:0] out_18,
  output [15:0] out_19,
  output [15:0] out_20,
  output [15:0] out_21,
  output [15:0] out_22,
  output out_23,
  output [15:0] out_24,
  output [15:0] out_25,
  output [15:0] out_26,
  output [15:0] out_27
);

  wire and_1_out, and_2_out, and_3_out, and_4_out, and_5_out, and_6_out, and_7_out, CLOCK, decoder_1_out1,
       decoder_1_out2, decoder_1_out3, decoder_1_out5, decoder_1_out6, decoder_1_out7, decoder_1_out9,
       decoder_1_out12, LD_out, LDR_out, Load_MEM_Input, Load_MEM_Output, not_1_out, or_1_out, or_2_out,
       or_3_out, or_4_out, or_5_out, or_6_out, or_7_out, or_8_out, or_9_out, or_10_out;
  wire [15:0] adder_1_out, adder_2_out, bit_extender_1_out, bit_extender_2_out, MEM_count_VALUE,
       multiplexer_3_out, multiplexer_4_out, PC_OUT_t, ram_1_data, SRC1_ALU, SRC2_ALU;

  Clock u_Clock (.out(CLOCK));
  and and_1 (and_1_out, IR_OUT[12], IR_OUT[13]);
  and and_2 (and_2_out, ~IR_OUT[12], ~IR_OUT[13], IR_OUT[14], IR_OUT[15]);  // AND_Gate
  and LD (LD_out, ~IR_OUT[15], ~IR_OUT[14], IR_OUT[13], ~IR_OUT[12]);  // AND_Gate
  Multiplexer #(.width(3), .enable("false")) multiplexer_1 (.in0(out_11), .in1(out_14), .out(out_17), .sel(and_1_out));
  Multiplexer #(.width(16), .enable("false")) multiplexer_2 (
    .in0(PC_OUT_t), .in1(out_19), .out(PC_OUT), .sel(and_2_out));
  or or_1 (or_1_out, LD_out, LDR_out);
  and LDR (LDR_out, ~IR_OUT[15], IR_OUT[14], IR_OUT[13], ~IR_OUT[12]);  // AND_Gate
  Registers_2 registers_2_1 (
    .Clock(CLOCK), .DST(out_14), .DST_VAL(out_24), .SRC1(out_17), .SRC2(out_13), .WE(out_23),
    .SRC1_OUTPUT(out_19), .SRC2_OUTPUT(out_20));
  ALU_2 alu_2_1 (.SRC1(SRC1_ALU), .SRC2(SRC2_ALU), .IR(IR_OUT), .OUTPUT(out_22));
  and and_3 (and_3_out, ~IR_OUT[15], IR_OUT[14], IR_OUT[13], IR_OUT[12]);  // AND_Gate
  and and_4 (and_4_out, ~IR_OUT[15], IR_OUT[14], IR_OUT[13], ~IR_OUT[12]);  // AND_Gate
  Multiplexer #(.width(16), .enable("false")) multiplexer_3 (
    .in0(out_22), .in1(MEM_count_VALUE), .out(multiplexer_3_out), .sel(or_1_out));
  Control_Unit_2 control_unit_2_1 (
    .CLOCK(CLOCK), .PC(PC_OUT), .IR(out_27), .IR_2(IR_OUT), .PC_2(PC_OUT_t), .STORE(out_2), .FETCH(out_3),
    .DECODE(out_5), .EVALUATE_ADDRESS(out_8), .FETCH_OPPERANDS(out_10), .EXECUTE(out_12));
  assign bit_extender_1_out = {{7{1'b0}}, out_15};  // Bit_Extender bit_extender_1
  assign bit_extender_2_out = {{10{1'b0}}, out_16};  // Bit_Extender bit_extender_2
  or or_2 (or_2_out, and_3_out, and_4_out);
  Register #(.width(16)) register_1 (.D(multiplexer_3_out), .en(out_12), .Q(out_24), .clk(CLOCK), .clr(out_3));
  Register #(.width(16)) register_2 (.D(out_25), .en(out_10), .Q(MEM_count_VALUE), .clk(CLOCK), .clr(out_3));
  Register #(.width(16)) register_3 (.D(out_20), .en(out_10), .Q(SRC2_ALU), .clk(CLOCK), .clr(out_3));
  Register #(.width(16)) register_4 (.D(out_19), .en(out_10), .Q(SRC1_ALU), .clk(CLOCK), .clr(out_3));
  Adder #(.width(16)) adder_1 (.a(adder_2_out), .b(multiplexer_4_out), .out(adder_1_out));  // open: cin, cout
  Adder #(.width(16)) adder_2 (.a(bit_extender_1_out), .b(bit_extender_2_out), .out(adder_2_out));  // open: cin, cout
  Multiplexer #(.width(16), .enable("false")) multiplexer_4 (
    .in0({16{1'b0}}), .in1(out_19), .out(multiplexer_4_out), .sel(or_2_out));
  Multiplexer #(.width(16), .enable("false")) multiplexer_5 (
    .in0(adder_1_out), .in1(PC_OUT), .out(out_26), .sel(out_3));
  Decoder #(.select(4), .enable("false")) decoder_1 (
    .out1(decoder_1_out1), .out2(decoder_1_out2), .out3(decoder_1_out3), .out5(decoder_1_out5),
    .out6(decoder_1_out6), .out7(decoder_1_out7), .out9(decoder_1_out9), .out12(decoder_1_out12),
    .sel(IR_OUT[15:12]));  // open: out0, out4, out8, out10, out11, out13, out14, out15
  or or_3 (or_3_out, decoder_1_out6, decoder_1_out7);
  or or_4 (or_4_out, decoder_1_out2, decoder_1_out6);
  RAM #(.addrWidth(16), .dataWidth(16), .bus("separate")) ram_1 (
    .addr(out_26), .din(out_19), .data(ram_1_data), .str(Load_MEM_Input), .clk(CLOCK), .ld(Load_MEM_Output));  // open: sel, clr
  or or_5 (or_5_out, decoder_1_out5, decoder_1_out1);
  or or_6 (or_6_out, decoder_1_out3, decoder_1_out2);
  or or_7 (or_7_out, decoder_1_out1, decoder_1_out9, decoder_1_out6, decoder_1_out5, decoder_1_out2);
  or or_8 (or_8_out, decoder_1_out3, decoder_1_out7);
  Demultiplexer #(.width(16), .enable("false")) demultiplexer_1 (
    .out0(out_25), .out1(out_27), .in(ram_1_data), .sel(out_3));
  or or_9 (or_9_out, decoder_1_out7, decoder_1_out9, decoder_1_out6, decoder_1_out12, decoder_1_out5, decoder_1_out1);
  and and_5 (and_5_out, or_7_out, out_2);
  and and_6 (and_6_out, or_4_out, out_10);
  and and_7 (and_7_out, or_8_out, out_2);
  Multiplexer #(.width(3), .enable("false")) multiplexer_6 (
    .in0(3'b000), .in1(IR_OUT[8:6]), .out(out_11), .sel(or_9_out));
  Multiplexer #(.width(3), .enable("false")) multiplexer_7 (
    .in0(3'b000), .in1(IR_OUT[2:0]), .out(out_13), .sel(or_5_out));
  Multiplexer #(.width(3), .enable("false")) multiplexer_8 (
    .in0(3'b000), .in1(IR_OUT[11:9]), .out(out_14), .sel(not_1_out));
  not not_1 (not_1_out, out_3);
  Multiplexer #(.width(9), .enable("false")) multiplexer_9 (
    .in0({9{1'b0}}), .in1(IR_OUT[8:0]), .out(out_15), .sel(or_6_out));
  Multiplexer #(.width(6), .enable("false")) multiplexer_10 (
    .in0({6{1'b0}}), .in1(IR_OUT[5:0]), .out(out_16), .sel(or_3_out));
  Multiplexer #(.enable("false")) multiplexer_11 (.in0(1'b0), .in1(1'b1), .out(out_23), .sel(and_5_out));
  Multiplexer #(.enable("false")) multiplexer_12 (.in0(1'b0), .in1(1'b1), .out(Load_MEM_Output), .sel(or_10_out));
  or or_10 (or_10_out, and_6_out, out_3);
  Multiplexer #(.enable("false")) multiplexer_13 (.in0(1'b0), .in1(1'b1), .out(Load_MEM_Input), .sel(and_7_out));
  assign out_21 = {{10{1'b0}}, IR_OUT[5:0]};  // Bit_Extender bit_extender_3

  assign out_6 = IR_OUT[15:12];
  assign out_7 = IR_OUT[13:12];
  assign out_9 = IR_OUT[15:14];
  assign out_18 = out_13;

  // Other names for the same wires on the sheet: Address[15:0] = out_26; ALU_RESULT[15:0] = out_22; DECODE = out_5;
  //   DST_VAL[15:0] = out_24; EVALUATE_ADDRESS = out_8; EXECUTE = out_12; FETCH = out_3; FETCH_OPPERANDS = out_10;
  //   Instruction[15:0] = out_27; IMMU5[5:0] = IR_OUT[5:0]; IR[15:0] = IR_OUT; OP1[1:0] = IR_OUT[13:12];
  //   OPCODE[3:0] = IR_OUT[15:12]; OP2[1:0] = IR_OUT[15:14]; MEM_count[15:0] = out_25; PC[15:0] = PC_OUT;
  //   PCoffset6[5:0] = out_16; PCoffsetf9[8:0] = out_15; REGISTER_WE = out_23; SR_DR[2:0] = out_14;
  //   SRC1[2:0] = out_17; SRC1_BaseR[2:0] = out_11; SRC1_REG[15:0] = out_19; SRC2[2:0] = out_13;
  //   SRC2_REG[15:0] = out_20; STORE = out_2

  // Notes on the sheet:
  //   Instruction Spliters
  //   Instruction Logic Circuits
  //   Register, Control Unit, ALU
  //   Instruction Cycle Temp Storage
  //   Memory
  //   LC-3 Final Project
  //   Decodes Instruction
  //   Bits 6-8
  //   Bits 0-2
  //   Bits 9-11
  //   Bits 0-8
  //   Bits 0-5
  //   Data Visualized
endmodule

// CONTROL
module Control_Unit_2 (
  input  CLOCK,
  input  [15:0] PC,
  input  [15:0] IR,
  output [15:0] IR_2,
  output [15:0] PC_2,
  output STORE,
  output FETCH,
  output DECODE,
  output EVALUATE_ADDRESS,
  output FETCH_OPPERANDS,
  output EXECUTE
);

  wire [2:0] counter_1_q;

  Counter #(.width(3), .max('h5)) counter_1 (.Q(counter_1_q), .clk(CLOCK));  // open: load, D, count, carry, clr
  Decoder #(.select(3)) decoder_1 (
    .out0(STORE), .out1(FETCH), .out2(DECODE), .out3(EVALUATE_ADDRESS), .out4(FETCH_OPPERANDS),
    .out5(EXECUTE), .sel(counter_1_q));  // open: out6, out7, en
  Register #(.width(16)) register_1 (.D(IR), .en(FETCH), .Q(IR_2), .clk(CLOCK));  // open: clr
  Counter #(.width(16), .max('hffff)) counter_2 (
    .load(FETCH), .D(PC), .count(DECODE), .Q(PC_2), .clk(CLOCK));  // open: carry, clr

  // Other names for the same wires on the sheet: Instruction[15:0] = IR

  // Notes on the sheet:
  //   Control Unit
endmodule

// ALU
module ALU_2 (
  input  [15:0] SRC1,
  input  [15:0] SRC2,
  input  [15:0] IR,
  output [15:0] OUTPUT
);

  wire [15:0] ADD, AND, EXTIMMU5, NOT, SRC2_t;

  assign EXTIMMU5 = {{11{1'b0}}, IR[4:0]};  // Bit_Extender bit_extender_1
  Adder #(.width(16)) adder_1 (.a(SRC1), .b(SRC2_t), .out(ADD));  // open: cin, cout
  assign AND = SRC1 & SRC2_t;  // AND_Gate and_1, 16 bits wide
  assign NOT = ~SRC1;  // NOT_Gate not_1, 16 bits wide
  Multiplexer #(.width(16)) multiplexer_1 (.in0(SRC2), .in1(EXTIMMU5), .out(SRC2_t), .sel(IR[5]));  // open: en
  Multiplexer #(.select(2), .width(16)) multiplexer_2 (
    .in0(ADD), .in1(AND), .in2(NOT), .in3(SRC1), .out(OUTPUT), .sel(IR[15:14]));  // open: en

  // Other names for the same wires on the sheet: IMMU5[4:0] = IR[4:0]; IMMEDIATE = IR[5]; ALUK[1:0] = IR[15:14];
  //   R2[15:0] = SRC2

  // Notes on the sheet:
  //   ALU
endmodule

// Registers
module Registers_2 (
  input  Clock,
  input  [2:0] DST,
  input  [15:0] DST_VAL,
  input  [2:0] SRC1,
  input  [2:0] SRC2,
  input  WE,
  output [15:0] SRC1_OUTPUT,
  output [15:0] SRC2_OUTPUT
);

  wire demultiplexer_1_out0, demultiplexer_1_out1, demultiplexer_1_out2, demultiplexer_1_out3,
       demultiplexer_1_out4, demultiplexer_1_out5, demultiplexer_1_out6, demultiplexer_1_out7;
  wire [15:0] R0_q, R1_q, R2_q, R3_q, R4_q, R5_q, R6_q, R7_q;

  Demultiplexer #(.select(3), .disabled(0), .enable("false")) demultiplexer_1 (
    .out0(demultiplexer_1_out0), .out1(demultiplexer_1_out1), .out2(demultiplexer_1_out2),
    .out3(demultiplexer_1_out3), .out4(demultiplexer_1_out4), .out5(demultiplexer_1_out5),
    .out6(demultiplexer_1_out6), .out7(demultiplexer_1_out7), .in(WE), .sel(DST));
  Register #(.width(16)) R0 (.D(DST_VAL), .en(demultiplexer_1_out0), .Q(R0_q), .clk(Clock));  // open: clr
  Register #(.width(16)) R1 (.D(DST_VAL), .en(demultiplexer_1_out1), .Q(R1_q), .clk(Clock));  // open: clr
  Register #(.width(16)) R2 (.D(DST_VAL), .en(demultiplexer_1_out2), .Q(R2_q), .clk(Clock));  // open: clr
  Register #(.width(16)) R3 (.D(DST_VAL), .en(demultiplexer_1_out3), .Q(R3_q), .clk(Clock));  // open: clr
  Register #(.width(16)) R4 (.D(DST_VAL), .en(demultiplexer_1_out4), .Q(R4_q), .clk(Clock));  // open: clr
  Register #(.width(16)) R5 (.D(DST_VAL), .en(demultiplexer_1_out5), .Q(R5_q), .clk(Clock));  // open: clr
  Register #(.width(16)) R6 (.D(DST_VAL), .en(demultiplexer_1_out6), .Q(R6_q), .clk(Clock));  // open: clr
  Register #(.width(16)) R7 (.D(DST_VAL), .en(demultiplexer_1_out7), .Q(R7_q), .clk(Clock));  // open: clr
  Multiplexer #(.select(3), .width(16), .enable("false")) multiplexer_1 (
    .in0(R0_q), .in1(R1_q), .in2(R2_q), .in3(R3_q), .in4(R4_q), .in5(R5_q), .in6(R6_q), .in7(R7_q),
    .out(SRC1_OUTPUT), .sel(SRC1));
  Multiplexer #(.select(3), .width(16), .enable("false")) multiplexer_2 (
    .in0(R0_q), .in1(R1_q), .in2(R2_q), .in3(R3_q), .in4(R4_q), .in5(R5_q), .in6(R6_q), .in7(R7_q),
    .out(SRC2_OUTPUT), .sel(SRC2));

  // Other names for the same wires on the sheet: C = Clock

  // Notes on the sheet:
  //   Registers
endmodule
